# Fritzing sketch Projeto (saved by Fritzing 0.9.3b)
breadboards: 1

parts:
  Q1 = NPN-Transistor [package="TO92 [THT]"]
  R1 = Resistor [tolerance=±5% resistance=220 package=THT]
  LED1 = LEDs [package=led10mm]
  Componente1 = Arduino Uno (Rev3)
  DHT1 = DHT11 Humitidy and Temperature Sensor (3 pins)
  Mod1 = MQ-7 breakout
  Mod2 = zmpt101b
  Mod3 = zmpt101b
  Grove1 = Grove Dust Sensor
  LCD1 = LCD screen
  R2 = Resistor [tolerance=±5% resistance=220 package=THT]
  Componente2 = Arduino Ethernet Shield (Rev3)

nets:
  N1: Q1.E, LED1.C
  N2: Q1.B, R1.Pin_1
  GND: Q1.C, Componente1.GND, DHT1.GND, Mod1.GND, Mod2.GND#3, Mod3.GND#3, Grove1.GND, LCD1.VSS, LCD1.V0, LCD1.R/W, R2.Pin_1
  N3: R1.Pin_0, Componente1.D3_PWM
  VCC: LED1.A, Componente1.5V, DHT1.VDD, Mod1.VCC, Mod2.VCC, Mod3.VCC, Grove1.VCC, LCD1.VDD, LCD1.LED+
  N4: Componente1.A0, DHT1.DATA
  N5: Componente1.A1, Mod1.AO
  N6: Componente1.A2, Mod2.OUT
  N7: Componente1.A3, Mod3.OUT
  N8: Componente1.A4/SDA, Grove1.SIG
  N9: Componente1.D8, LCD1.E
  N10: Componente1.D9_PWM, LCD1.RS
  N11: Componente1.D10_PWM/SS, Componente2.ETH_CS
  N12: Componente1.D11_PWM/MOSI, Componente2.PWM_D11
  N13: Componente1.D12/MISO, Componente2.SPI/D12
  N14: Componente1.D13/SCK, Componente2.SPI/D13
  N15: Componente1.D2, Grove1.NC
  N16: Componente1.D4, LCD1.DB7
  N17: Componente1.D5_PWM, LCD1.DB6
  N18: Componente1.D6_PWM, LCD1.DB5
  N19: Componente1.D7, LCD1.DB4
  N20: LCD1.LED-, R2.Pin_0

notes:
  - / +
  Emissor infravermelho
  S / + / -
  dht11 ou 22
  VCC / GND / D0 / A0
  MQ-Variantes
  zmpt101b
  GND / GND / OUT / VCC
  dsn501a
  Controle (Vout1) / Vout2 / VCC / Vout1 / GND
  Transistor
  222A
  220Ω resistor ou até 150Ω para maior intensidade
  Importante:
  Transitor 2N2222 e resistor 470Ω são recomendados pelo projeto original

custom parts:
  DHT11 Humitidy and Temperature Sensor (3 pins): DHT11 Humidity and Temperature Sensor (3 pins) from the design created by John De Cristofaro for Adafruit Industries.
  MQ-7 breakout: MQ-5 gas sensor
  zmpt101b: Single phase ac active output voltate transformer module.
  Grove Dust Sensor: PPD42 Grove Dust Sensor
